# Fritzing sketch AHT Sketch (saved by Fritzing 1.0.1rc)

parts:
  ESP8266 = Amica NodeMCU DEVKIT 1.0
  AHT10 = AHT10 Temperature and Humidity Sensor

nets:
  N1: ESP8266.pin_9, AHT10.GND
  N2: ESP8266.pin_10, AHT10.VIN
  N3: ESP8266.pin_13, AHT10.SDA
  N4: ESP8266.pin_14, AHT10.SCL

notes:
  # ESP8266 to AHT10
  GND to GND
  3V3 to VIN
  D1 to SCL
  D2 to SDA
